# Fritzing sketch DCmotor1 (saved by Fritzing 0.8.3b)
breadboards: 1

parts:
  元件1 = Arduino Uno (Rev3)
  R1 = Resistor [tolerance=±5% resistance=470 package=THT]
  D1 = Rectifier Diode [part_number=1N4001 package="300 mil [THT]"]
  M1 = DC Motor

nets:
  N1: 元件1.GND, M1.pin_1
  N2: 元件1.5V, R1.Pin_0
  N3: R1.Pin_1, D1.cathode
  N4: D1.anode, M1.pin_2
